// Digital circuit 00-IF-DR-register.dig as structural Verilog
module _00_IF_DR_register (
  input  [31:0] IW_0,
  input  [63:0] PC_0,
  input  [63:0] PC4_0,
  input  CLK,
  input  EN,
  input  CLR,
  output [31:0] IW_1,
  output [63:0] PC_1,
  output [63:0] PC4_1
);

  register_with_clr_32bits register_with_clr_32bits_1 (.D(IW_0), .CLK(CLK), .EN(EN), .CLR(CLR), .Q(IW_1));
  register_with_clr_64bits register_with_clr_64bits_1 (.D(PC_0), .CLK(CLK), .EN(EN), .CLR(CLR), .Q(PC_1));
  register_with_clr_64bits register_with_clr_64bits_2 (.D(PC4_0), .CLK(CLK), .EN(EN), .CLR(CLR), .Q(PC4_1));
endmodule
