// Digital circuit 01-DR-EX-register.dig as structural Verilog
module _01_DR_EX_register (
  input  [1:0] MSZ_1,
  input  [2:0] BUOp_1,
  input  CLK,
  input  EN,
  input  CLR,
  input  WDsl_1,
  input  [31:0] IW_1,
  input  [63:0] RD0_1,
  input  [63:0] RD1_1,
  input  [4:0] RR0_1,
  input  [4:0] RR1_1,
  input  [2:0] ALUB_1,
  input  PCsl_1,
  input  [63:0] PC_1,
  input  MST_1,
  input  MLD_1,
  input  MR_1,
  input  ALUA_1,
  input  [3:0] ALOp_1,
  input  RFW_1,
  input  [4:0] WR_1,
  input  [63:0] PC4_1,
  output [1:0] MSZ_2,
  output [2:0] BUOp_2,
  output WDsl_2,
  output [31:0] IW_2,
  output [63:0] RD0_2,
  output [63:0] RD1_2,
  output [4:0] RR0_2,
  output [4:0] RR1_2,
  output PCsl_2,
  output [2:0] ALUB_2,
  output [63:0] PC_2,
  output MST_2,
  output MLD_2,
  output MR_2,
  output ALUA_2,
  output [3:0] ALOp_2,
  output RFW_2,
  output [4:0] WR_2,
  output [63:0] PC4_2
);

  register_with_clr_32bits register_with_clr_32bits_1 (.D(IW_1), .CLK(CLK), .EN(EN), .CLR(CLR), .Q(IW_2));
  register_with_clr_05bits register_with_clr_05bits_1 (.D(RR0_1), .CLK(CLK), .EN(EN), .CLR(CLR), .Q(RR0_2));
  register_with_clr_05bits register_with_clr_05bits_2 (.D(RR1_1), .CLK(CLK), .EN(EN), .CLR(CLR), .Q(RR1_2));
  register_with_clr_05bits register_with_clr_05bits_3 (.D(WR_1), .CLK(CLK), .EN(EN), .CLR(CLR), .Q(WR_2));
  register_with_clr_64bits register_with_clr_64bits_1 (.D(RD0_1), .CLK(CLK), .EN(EN), .CLR(CLR), .Q(RD0_2));
  register_with_clr_64bits register_with_clr_64bits_2 (.D(RD1_1), .CLK(CLK), .EN(EN), .CLR(CLR), .Q(RD1_2));
  register_with_clr_64bits register_with_clr_64bits_3 (.D(PC_1), .CLK(CLK), .EN(EN), .CLR(CLR), .Q(PC_2));
  register_with_clr_64bits register_with_clr_64bits_4 (.D(PC4_1), .CLK(CLK), .EN(EN), .CLR(CLR), .Q(PC4_2));
  register_with_clr_02bits register_with_clr_02bits_1 (.D(MSZ_1), .CLK(CLK), .EN(EN), .CLR(CLR), .Q(MSZ_2));
  register_with_clr_01bits register_with_clr_01bits_1 (.D(MST_1), .CLK(CLK), .EN(EN), .CLR(CLR), .Q(MST_2));
  register_with_clr_01bits register_with_clr_01bits_2 (.D(MLD_1), .CLK(CLK), .EN(EN), .CLR(CLR), .Q(MLD_2));
  register_with_clr_01bits register_with_clr_01bits_3 (.D(MR_1), .CLK(CLK), .EN(EN), .CLR(CLR), .Q(MR_2));
  register_with_clr_03bits register_with_clr_03bits_1 (.D(BUOp_1), .CLK(CLK), .EN(EN), .CLR(CLR), .Q(BUOp_2));
  register_with_clr_01bits register_with_clr_01bits_4 (.D(WDsl_1), .CLK(CLK), .EN(EN), .CLR(CLR), .Q(WDsl_2));
  register_with_clr_01bits register_with_clr_01bits_5 (.D(PCsl_1), .CLK(CLK), .EN(EN), .CLR(CLR), .Q(PCsl_2));
  register_with_clr_03bits register_with_clr_03bits_2 (.D(ALUB_1), .CLK(CLK), .EN(EN), .CLR(CLR), .Q(ALUB_2));
  register_with_clr_01bits register_with_clr_01bits_6 (.D(ALUA_1), .CLK(CLK), .EN(EN), .CLR(CLR), .Q(ALUA_2));
  register_with_clr_04bits register_with_clr_04bits_1 (.D(ALOp_1), .CLK(CLK), .EN(EN), .CLR(CLR), .Q(ALOp_2));
  register_with_clr_01bits register_with_clr_01bits_7 (.D(RFW_1), .CLK(CLK), .EN(EN), .CLR(CLR), .Q(RFW_2));
endmodule
