// Digital circuit 02-EX-MEM-register.dig as structural Verilog
module _02_EX_MEM_register (
  input  [1:0] MSZ_2,
  input  CLK,
  input  EN,
  input  CLR,
  input  WDsl_2,
  input  [31:0] IW_2,
  input  [63:0] ALUR_2,
  input  [63:0] RD1_2,
  input  [4:0] RR0_2,
  input  [4:0] RR1_2,
  input  PCbr_2,
  input  MST_2,
  input  MLD_2,
  input  MR_2,
  input  RFW_2,
  input  [4:0] WR_2,
  input  [63:0] PC4_2,
  output [1:0] MSZ_3,
  output WDsl_3,
  output [31:0] IW_3,
  output [63:0] ALUR_3,
  output [63:0] RD1_3,
  output [4:0] RR0_3,
  output [4:0] RR1_3,
  output PCbr_3,
  output MST_3,
  output MLD_3,
  output MR_3,
  output RFW_3,
  output [4:0] WR_3,
  output [63:0] PC4_3
);

  register_with_clr_32bits register_with_clr_32bits_1 (.D(IW_2), .CLK(CLK), .EN(EN), .CLR(CLR), .Q(IW_3));
  register_with_clr_05bits register_with_clr_05bits_1 (.D(RR0_2), .CLK(CLK), .EN(EN), .CLR(CLR), .Q(RR0_3));
  register_with_clr_05bits register_with_clr_05bits_2 (.D(RR1_2), .CLK(CLK), .EN(EN), .CLR(CLR), .Q(RR1_3));
  register_with_clr_05bits register_with_clr_05bits_3 (.D(WR_2), .CLK(CLK), .EN(EN), .CLR(CLR), .Q(WR_3));
  register_with_clr_64bits register_with_clr_64bits_1 (.D(ALUR_2), .CLK(CLK), .EN(EN), .CLR(CLR), .Q(ALUR_3));
  register_with_clr_64bits register_with_clr_64bits_2 (.D(RD1_2), .CLK(CLK), .EN(EN), .CLR(CLR), .Q(RD1_3));
  register_with_clr_64bits register_with_clr_64bits_3 (.D(PC4_2), .CLK(CLK), .EN(EN), .CLR(CLR), .Q(PC4_3));
  register_with_clr_02bits register_with_clr_02bits_1 (.D(MSZ_2), .CLK(CLK), .EN(EN), .CLR(CLR), .Q(MSZ_3));
  register_with_clr_01bits register_with_clr_01bits_1 (.D(MST_2), .CLK(CLK), .EN(EN), .CLR(CLR), .Q(MST_3));
  register_with_clr_01bits register_with_clr_01bits_2 (.D(MLD_2), .CLK(CLK), .EN(EN), .CLR(CLR), .Q(MLD_3));
  register_with_clr_01bits register_with_clr_01bits_3 (.D(MR_2), .CLK(CLK), .EN(EN), .CLR(CLR), .Q(MR_3));
  register_with_clr_01bits register_with_clr_01bits_4 (.D(WDsl_2), .CLK(CLK), .EN(EN), .CLR(CLR), .Q(WDsl_3));
  register_with_clr_01bits register_with_clr_01bits_5 (.D(PCbr_2), .CLK(CLK), .EN(EN), .CLR(CLR), .Q(PCbr_3));
  register_with_clr_01bits register_with_clr_01bits_6 (.D(RFW_2), .CLK(CLK), .EN(EN), .CLR(CLR), .Q(RFW_3));
endmodule
