// Digital circuit 03-MEM-WB-register.dig as structural Verilog
module _03_MEM_WB_register (
  input  CLK,
  input  EN,
  input  CLR,
  input  WDsl_3,
  input  [31:0] IW_3,
  input  [63:0] ALUR_3,
  input  [63:0] MRD_3,
  input  [4:0] RR0_3,
  input  [4:0] RR1_3,
  input  PCbr_3,
  input  MR_3,
  input  RFW_3,
  input  [4:0] WR_3,
  input  [63:0] PC4_3,
  output WDsl_4,
  output [31:0] IW_4,
  output [63:0] ALUR_4,
  output [63:0] MRD_4,
  output [4:0] RR0_4,
  output [4:0] RR1_4,
  output PCbr_4,
  output MR_4,
  output RFW_4,
  output [4:0] WR_4,
  output [63:0] PC4_4
);

  register_with_clr_32bits register_with_clr_32bits_1 (.D(IW_3), .CLK(CLK), .EN(EN), .CLR(CLR), .Q(IW_4));
  register_with_clr_05bits register_with_clr_05bits_1 (.D(RR0_3), .CLK(CLK), .EN(EN), .CLR(CLR), .Q(RR0_4));
  register_with_clr_05bits register_with_clr_05bits_2 (.D(RR1_3), .CLK(CLK), .EN(EN), .CLR(CLR), .Q(RR1_4));
  register_with_clr_05bits register_with_clr_05bits_3 (.D(WR_3), .CLK(CLK), .EN(EN), .CLR(CLR), .Q(WR_4));
  register_with_clr_64bits register_with_clr_64bits_1 (.D(ALUR_3), .CLK(CLK), .EN(EN), .CLR(CLR), .Q(ALUR_4));
  register_with_clr_64bits register_with_clr_64bits_2 (.D(MRD_3), .CLK(CLK), .EN(EN), .CLR(CLR), .Q(MRD_4));
  register_with_clr_64bits register_with_clr_64bits_3 (.D(PC4_3), .CLK(CLK), .EN(EN), .CLR(CLR), .Q(PC4_4));
  register_with_clr_01bits register_with_clr_01bits_1 (.D(MR_3), .CLK(CLK), .EN(EN), .CLR(CLR), .Q(MR_4));
  register_with_clr_01bits register_with_clr_01bits_2 (.D(WDsl_3), .CLK(CLK), .EN(EN), .CLR(CLR), .Q(WDsl_4));
  register_with_clr_01bits register_with_clr_01bits_3 (.D(PCbr_3), .CLK(CLK), .EN(EN), .CLR(CLR), .Q(PCbr_4));
  register_with_clr_01bits register_with_clr_01bits_4 (.D(RFW_3), .CLK(CLK), .EN(EN), .CLR(CLR), .Q(RFW_4));
endmodule
