// Digital circuit alu.dig as structural Verilog
module alu (
  input  [63:0] A,
  input  [63:0] B,
  input  [3:0] ALUop,
  output [63:0] R
);

  wire [31:0] addw_s;
  wire [63:0] add_s, and_1_out, bitextender_1_out, mul_mul, or_1_out, sll_out, sra_out, srl_out, sub_s;

  Add #(.Bits(64)) add (.a(A), .b(B), .c_i(1'b0), .s(add_s));  // open: c_o
  Sub #(.Bits(64)) sub (.a(A), .b(B), .c_i(1'b0), .s(sub_s));  // open: c_o
  Mul #(.Bits(32)) mul (.a(A[31:0]), .b(B[31:0]), .mul(mul_mul));
  BarrelShifter #(.Bits(64)) sll (.in(A), .shift(B[6:0]), .out(sll_out));
  BarrelShifter #(.Bits(64), .direction("right")) srl (.in(A), .shift(B[6:0]), .out(srl_out));
  BarrelShifter #(.Bits(64), .barrelShifterMode("arithmetic"), .direction("right")) sra (
    .in(B), .shift(A[6:0]), .out(sra_out));
  Add #(.Bits(32)) addw (.a(A[31:0]), .b(B[31:0]), .c_i(1'b0), .s(addw_s));  // open: c_o
  assign or_1_out = A | B;  // Or or_1, 64 bits wide
  assign and_1_out = A & B;  // And and_1, 64 bits wide
  BitExtender #(.inputBits(32), .outputBits(64)) bitextender_1 (.in(addw_s), .out(bitextender_1_out));
  Multiplexer #(.Selector_Bits(4), .Bits(64)) multiplexer_1 (
    .sel(ALUop), .in_0(add_s), .in_1(sub_s), .in_2(mul_mul), .in_3(sll_out), .in_4(srl_out), .in_5(sra_out),
    .in_6(B), .in_7(bitextender_1_out), .in_8(or_1_out), .in_9(and_1_out), .in_10({64{1'b0}}),
    .in_11({64{1'b0}}), .in_12({64{1'b0}}), .in_13({64{1'b0}}), .in_14({64{1'b0}}), .in_15({64{1'b0}}),
    .out(R));

  // Notes on the sheet:
  //   lui
endmodule
