// Digital circuit branch-unit.dig as structural Verilog
module branch_unit (
  input  [63:0] A,
  input  [63:0] B,
  input  PCsel,
  input  [2:0] BUOp,
  output PCbr
);

  wire beq_eq, bge_eq, bge_gt, blt_lt, bne_eq, multiplexer_1_out, not_1_out, or_1_out;

  Comparator #(.Bits(64)) beq (.a(A), .b(B), .eq(beq_eq));  // open: gt, lt
  Comparator #(.Bits(64)) bne (.a(A), .b(B), .eq(bne_eq));  // open: gt, lt
  Comparator #(.Bits(64)) blt (.a(A), .b(B), .lt(blt_lt));  // open: gt, eq
  Comparator #(.Bits(64)) bge (.a(A), .b(B), .gt(bge_gt), .eq(bge_eq));  // open: lt
  not not_1 (not_1_out, bne_eq);
  or or_1 (or_1_out, bge_gt, bge_eq);
  Multiplexer #(.Selector_Bits(3)) multiplexer_1 (
    .sel(BUOp), .in_0(1'b0), .in_1(beq_eq), .in_2(not_1_out), .in_3(blt_lt), .in_4(or_1_out), .in_5(1'b0),
    .in_6(1'b0), .in_7(1'b0), .out(multiplexer_1_out));
  or or_2 (PCbr, multiplexer_1_out, PCsel);
endmodule
