// Digital circuit decoder-inst.dig as structural Verilog
module decoder_inst (
  input  [31:0] IW,
  output ALUSrcA,
  output [3:0] ALUOp,
  output RFW,
  output [2:0] ALUSrcB,
  output PCsel,
  output WDsel,
  output [2:0] BUOp,
  output [1:0] SZ,
  output ST,
  output LD,
  output MR
);

  wire [4:0] decoder_inum_1_inum;

  decoder_inum decoder_inum_1 (.IW(IW), .INUM(decoder_inum_1_inum));
  ROM #(.AddrBits(5), .Bits(19)) rom_1 (
    .A(decoder_inum_1_inum), .sel(1'b1),
    .D({RFW, ALUOp, ALUSrcA, ALUSrcB, PCsel, WDsel, BUOp, MR, LD, ST, SZ}));

  // Notes on the sheet:
  //   contents of rom_1 (hex, n*v repeats v):
  //   40400,60400,64400,4d400,51400,55400,40000,44000,4c000,50000,54000
  //   ,60000,64000,48000,5c400,58c00,42b00,40700,3020,3040,3060,3080
  //   ,40418,4041a,4041b,180c,180e,180f
endmodule
