// Digital circuit decoder-inum.dig as structural Verilog
module decoder_inum (
  input  [31:0] IW,
  output [4:0] INUM
);

  wire addi, addr, adiw, andi, andr, beq, bge, blt, bne, jal, jalr, lb, ld, lui, lw, mulr, none, nop, ori,
       orr, sb, sd, slli, sllr, srai, srar, srli, srlr, subr, sw, unimp;

  eq_i_type eq_i_type_1 (.iw_opcode(IW[6:0]), .iw_funct3(IW[14:12]), .opcode(7'b0010011), .funct3(3'b000), .eq(addi));
  eq_i_type eq_i_type_2 (.iw_opcode(IW[6:0]), .iw_funct3(IW[14:12]), .opcode(7'b0010011), .funct3(3'b110), .eq(ori));
  eq_i_type eq_i_type_3 (.iw_opcode(IW[6:0]), .iw_funct3(IW[14:12]), .opcode(7'b0010011), .funct3(3'b111), .eq(andi));
  eq_i_type_sh_eq eq_i_type_sh_eq_1 (
    .iw_opcode(IW[6:0]), .iw_funct3(IW[14:12]), .iw_funct6(IW[31:26]), .opcode(7'b0010011), .funct3(3'b001),
    .funct6({6{1'b0}}), .eq(slli));
  eq_i_type_sh_eq eq_i_type_sh_eq_2 (
    .iw_opcode(IW[6:0]), .iw_funct3(IW[14:12]), .iw_funct6(IW[31:26]), .opcode(7'b0010011), .funct3(3'b101),
    .funct6({6{1'b0}}), .eq(srli));
  eq_i_type_sh_eq eq_i_type_sh_eq_3 (
    .iw_opcode(IW[6:0]), .iw_funct3(IW[14:12]), .iw_funct6(IW[31:26]), .opcode(7'b0010011), .funct3(3'b101),
    .funct6(6'b010000), .eq(srai));
  eq_r_type eq_r_type_1 (
    .iw_opcode(IW[6:0]), .iw_funct3(IW[14:12]), .iw_funct7(IW[31:25]), .opcode(7'b0110011), .funct3(3'b000),
    .funct7({7{1'b0}}), .eq(addr));
  eq_r_type eq_r_type_2 (
    .iw_opcode(IW[6:0]), .iw_funct3(IW[14:12]), .iw_funct7(IW[31:25]), .opcode(7'b0110011), .funct3(3'b000),
    .funct7(7'b0100000), .eq(subr));
  eq_r_type eq_r_type_3 (
    .iw_opcode(IW[6:0]), .iw_funct3(IW[14:12]), .iw_funct7(IW[31:25]), .opcode(7'b0110011), .funct3(3'b001),
    .funct7({7{1'b0}}), .eq(sllr));
  eq_r_type eq_r_type_4 (
    .iw_opcode(IW[6:0]), .iw_funct3(IW[14:12]), .iw_funct7(IW[31:25]), .opcode(7'b0110011), .funct3(3'b101),
    .funct7({7{1'b0}}), .eq(srlr));
  eq_r_type eq_r_type_5 (
    .iw_opcode(IW[6:0]), .iw_funct3(IW[14:12]), .iw_funct7(IW[31:25]), .opcode(7'b0110011), .funct3(3'b101),
    .funct7(7'b0100000), .eq(srar));
  eq_r_type eq_r_type_6 (
    .iw_opcode(IW[6:0]), .iw_funct3(IW[14:12]), .iw_funct7(IW[31:25]), .opcode(7'b0110011), .funct3(3'b110),
    .funct7({7{1'b0}}), .eq(orr));
  eq_r_type eq_r_type_7 (
    .iw_opcode(IW[6:0]), .iw_funct3(IW[14:12]), .iw_funct7(IW[31:25]), .opcode(7'b0110011), .funct3(3'b111),
    .funct7({7{1'b0}}), .eq(andr));
  eq_r_type eq_r_type_8 (
    .iw_opcode(IW[6:0]), .iw_funct3(IW[14:12]), .iw_funct7(IW[31:25]), .opcode(7'b0110011), .funct3(3'b000),
    .funct7(7'b0000001), .eq(mulr));
  eq_i_type eq_i_type_4 (.iw_opcode(IW[6:0]), .iw_funct3(IW[14:12]), .opcode(7'b0011011), .funct3(3'b000), .eq(adiw));
  Comparator #(.Bits(7)) u_lui (.a(IW[6:0]), .b(7'b0110111), .eq(lui));  // open: gt, lt
  Comparator #(.Bits(7)) u_jal (.a(IW[6:0]), .b(7'b1101111), .eq(jal));  // open: gt, lt
  eq_i_type eq_i_type_5 (.iw_opcode(IW[6:0]), .iw_funct3(IW[14:12]), .opcode(7'b1100111), .funct3(3'b000), .eq(jalr));
  eq_i_type eq_i_type_6 (.iw_opcode(IW[6:0]), .iw_funct3(IW[14:12]), .opcode(7'b1100011), .funct3(3'b000), .eq(beq));
  eq_i_type eq_i_type_7 (.iw_opcode(IW[6:0]), .iw_funct3(IW[14:12]), .opcode(7'b1100011), .funct3(3'b001), .eq(bne));
  eq_i_type eq_i_type_8 (.iw_opcode(IW[6:0]), .iw_funct3(IW[14:12]), .opcode(7'b1100011), .funct3(3'b100), .eq(blt));
  eq_i_type eq_i_type_9 (.iw_opcode(IW[6:0]), .iw_funct3(IW[14:12]), .opcode(7'b1100011), .funct3(3'b101), .eq(bge));
  eq_i_type eq_i_type_10 (.iw_opcode(IW[6:0]), .iw_funct3(IW[14:12]), .opcode(7'b0000011), .funct3(3'b000), .eq(lb));
  eq_i_type eq_i_type_11 (.iw_opcode(IW[6:0]), .iw_funct3(IW[14:12]), .opcode(7'b0000011), .funct3(3'b010), .eq(lw));
  eq_i_type eq_i_type_12 (.iw_opcode(IW[6:0]), .iw_funct3(IW[14:12]), .opcode(7'b0000011), .funct3(3'b011), .eq(ld));
  eq_i_type eq_i_type_13 (.iw_opcode(IW[6:0]), .iw_funct3(IW[14:12]), .opcode(7'b0100011), .funct3(3'b000), .eq(sb));
  eq_i_type eq_i_type_14 (.iw_opcode(IW[6:0]), .iw_funct3(IW[14:12]), .opcode(7'b0100011), .funct3(3'b010), .eq(sw));
  eq_i_type eq_i_type_15 (.iw_opcode(IW[6:0]), .iw_funct3(IW[14:12]), .opcode(7'b0100011), .funct3(3'b011), .eq(sd));
  Comparator #(.Bits(32)) u_unimp (.a(IW), .b(32'hc0001073), .eq(unimp));  // open: gt, lt
  Comparator #(.Bits(32)) u_nop (.a(IW), .b(32'h13), .eq(nop));  // open: gt, lt
  Comparator #(.Bits(32)) u_none (.a(IW), .b({32{1'b0}}), .eq(none));  // open: gt, lt
  PriorityEncoder #(.Selector_Bits(5)) u_INUM (
    .in0(addi), .in1(ori), .in2(andi), .in3(slli), .in4(srli), .in5(srai), .in6(addr), .in7(subr),
    .in8(sllr), .in9(srlr), .in10(srar), .in11(orr), .in12(andr), .in13(mulr), .in14(adiw), .in15(lui),
    .in16(jal), .in17(jalr), .in18(beq), .in19(bne), .in20(blt), .in21(bge), .in22(lb), .in23(lw), .in24(ld),
    .in25(sb), .in26(sw), .in27(sd), .in28(unimp), .in29(nop), .in30(none), .in31(1'b0), .num(INUM));  // open: any

  // Other names for the same wires on the sheet: opcode[6:0] = IW[6:0]; funct3[2:0] = IW[14:12];
  //   funct7[6:0] = IW[31:25]; funct6[5:0] = IW[31:26]
endmodule
