// Digital circuit eq-i-type.dig as structural Verilog
module eq_i_type (
  input  [6:0] iw_opcode,
  input  [2:0] iw_funct3,
  input  [6:0] opcode,
  input  [2:0] funct3,
  output eq
);

  wire funct3_eq_eq, opcode_eq_eq;

  Comparator #(.Bits(7)) opcode_eq (.a(iw_opcode), .b(opcode), .eq(opcode_eq_eq));  // open: gt, lt
  Comparator #(.Bits(3)) funct3_eq (.a(iw_funct3), .b(funct3), .eq(funct3_eq_eq));  // open: gt, lt
  and and_1 (eq, opcode_eq_eq, funct3_eq_eq);
endmodule
