// Digital circuit iw-to-ascii.dig as structural Verilog
module iw_to_ascii (
  input  [31:0] IW,
  output [7:0] I_3,
  output [7:0] I_2,
  output [7:0] I_1,
  output [7:0] I_0
);

  wire [4:0] decoder_inum_1_inum;

  decoder_inum decoder_inum_1 (.IW(IW), .INUM(decoder_inum_1_inum));
  ROM #(.AddrBits(5), .Bits(32)) rom_1 (.A(decoder_inum_1_inum), .sel(1'b1), .D({I_0, I_1, I_2, I_3}));
  // Probe on I_0
  // Probe on I_1
  // Probe on I_2
  // Probe on I_3

  // Notes on the sheet:
  //   contents of rom_1 (hex, n*v repeats v):
  //   41444449,4f52495f,414e4449,534c4c49,53524c49,53524149,41444452
  //   ,53554252,534c4c5f,53524c5f,5352415f,4f525f5f,414e445f,4d554c52
  //   ,41444957,4c55495f,4a414c5f,4a414c52,4245515f,424e455f,424c545f
  //   ,4247455f,4c425f5f,4c575f5f,4c445f5f,53425f5f,53575f5f,53445f5f
  //   ,554e494d,4e4f505f,4e4f4e45
endmodule
