// Digital circuit mem-inst-p06.dig as structural Verilog
module mem_inst_p06 (
  input  [7:0] ADDR,
  input  [4:0] PROG,
  output [31:0] IW
);

  wire [31:0] _00, _01, _02, _03, _04, _05, _06, _07, _08, _09, _10, _11, _12, _13, _14, _15, _16, _17, _18,
       _19, _20, _21, _22, _23;

  ROM #(.AddrBits(8), .Bits(32)) _00_add_r (.A(ADDR), .sel(1'b1), .D(_00));
  ROM #(.AddrBits(8), .Bits(32)) _01_add_i (.A(ADDR), .sel(1'b1), .D(_01));
  ROM #(.AddrBits(8), .Bits(32)) _02_sll_r (.A(ADDR), .sel(1'b1), .D(_02));
  ROM #(.AddrBits(8), .Bits(32)) _03_sll_i (.A(ADDR), .sel(1'b1), .D(_03));
  ROM #(.AddrBits(8), .Bits(32)) _04_srl_r (.A(ADDR), .sel(1'b1), .D(_04));
  ROM #(.AddrBits(8), .Bits(32)) _05_srl_i (.A(ADDR), .sel(1'b1), .D(_05));
  ROM #(.AddrBits(8), .Bits(32)) _06_sd_ld (.A(ADDR), .sel(1'b1), .D(_06));
  ROM #(.AddrBits(8), .Bits(32)) _07_sw_lw (.A(ADDR), .sel(1'b1), .D(_07));
  ROM #(.AddrBits(8), .Bits(32)) _08_jal (.A(ADDR), .sel(1'b1), .D(_08));
  ROM #(.AddrBits(8), .Bits(32)) _09_j (.A(ADDR), .sel(1'b1), .D(_09));
  ROM #(.AddrBits(8), .Bits(32)) _10_beq (.A(ADDR), .sel(1'b1), .D(_10));
  ROM #(.AddrBits(8), .Bits(32)) _11_blt (.A(ADDR), .sel(1'b1), .D(_11));
  ROM #(.AddrBits(8), .Bits(32)) _12_bge (.A(ADDR), .sel(1'b1), .D(_12));
  ROM #(.AddrBits(8), .Bits(32)) _13_mul (.A(ADDR), .sel(1'b1), .D(_13));
  ROM #(.AddrBits(8), .Bits(32)) _14_lui (.A(ADDR), .sel(1'b1), .D(_14));
  ROM #(.AddrBits(8), .Bits(32)) _15_sb_lb (.A(ADDR), .sel(1'b1), .D(_15));
  ROM #(.AddrBits(8), .Bits(32)) _16_quadratic (.A(ADDR), .sel(1'b1), .D(_16));
  ROM #(.AddrBits(8), .Bits(32)) _17_get_bitseq (.A(ADDR), .sel(1'b1), .D(_17));
  ROM #(.AddrBits(8), .Bits(32)) _18_max3 (.A(ADDR), .sel(1'b1), .D(_18));
  ROM #(.AddrBits(8), .Bits(32)) _19_fib_rec (.A(ADDR), .sel(1'b1), .D(_19));
  ROM #(.AddrBits(8), .Bits(32)) _20_is_pal (.A(ADDR), .sel(1'b1), .D(_20));
  ROM #(.AddrBits(8), .Bits(32)) _21_to_upper (.A(ADDR), .sel(1'b1), .D(_21));
  ROM #(.AddrBits(8), .Bits(32)) _22_sort (.A(ADDR), .sel(1'b1), .D(_22));
  ROM #(.AddrBits(8), .Bits(32)) _23_merge_sort (.A(ADDR), .sel(1'b1), .D(_23));
  Multiplexer #(.Selector_Bits(5), .Bits(32)) multiplexer_1 (
    .sel(PROG), .in_0(_00), .in_1(_01), .in_2(_02), .in_3(_03), .in_4(_04), .in_5(_05), .in_6(_06),
    .in_7(_07), .in_8(_08), .in_9(_09), .in_10(_10), .in_11(_11), .in_12(_12), .in_13(_13), .in_14(_14),
    .in_15(_15), .in_16(_16), .in_17(_17), .in_18(_18), .in_19(_19), .in_20(_20), .in_21(_21), .in_22(_22),
    .in_23(_23), .in_24({32{1'b0}}), .in_25({32{1'b0}}), .in_26({32{1'b0}}), .in_27({32{1'b0}}),
    .in_28({32{1'b0}}), .in_29({32{1'b0}}), .in_30({32{1'b0}}), .in_31({32{1'b0}}), .out(IW));

  // Notes on the sheet:
  //   contents of _00_add_r (hex, n*v repeats v):
  //   100513,200593,b50633,c0001073
  //   contents of _01_add_i (hex, n*v repeats v):
  //   100513,250613,c0001073
  //   contents of _02_sll_r (hex, n*v repeats v):
  //   100593,200613,c59533,c0001073
  //   contents of _03_sll_i (hex, n*v repeats v):
  //   100593,359513,c0001073
  //   contents of _04_srl_r (hex, n*v repeats v):
  //   800593,100613,c5d533,c0001073
  //   contents of _05_srl_i (hex, n*v repeats v):
  //   2000593,25d513,c0001073
  //   contents of _06_sd_ld (hex, n*v repeats v):
  //   8000113,ff810113,513,6300293,513023,13503,c0001073
  //   contents of _07_sw_lw (hex, n*v repeats v):
  //   8000113,ff810113,513,6300293,512023,12503,c0001073
  //   contents of _08_jal (hex, n*v repeats v):
  //   100513,200593,8000ef,c0001073,b50533,8067
  //   contents of _09_j (hex, n*v repeats v):
  //   100513,80006f,513,c0001073
  //   contents of _10_beq (hex, n*v repeats v):
  //   100513,100593,b50463,513,c0001073
  //   contents of _11_blt (hex, n*v repeats v):
  //   100513,200593,b54463,513,c0001073
  //   contents of _12_bge (hex, n*v repeats v):
  //   200513,100593,b55463,513,c0001073
  //   contents of _13_mul (hex, n*v repeats v):
  //   300513,300593,2b50533,c0001073
  //   contents of _14_lui (hex, n*v repeats v):
  //   1537,c0001073
  //   contents of _15_sb_lb (hex, n*v repeats v):
  //   8000113,ff810113,513,6300293,5101a3,310503,c0001073
  //   contents of _16_quadratic (hex, n*v repeats v):
  //   200513,300593,400613,500693,8000ef,c0001073,2a502b3,2b282b3,2c50333
  //   ,628533,d50533,8067
  //   contents of _17_get_bitseq (hex, n*v repeats v):
  //   17537,fa55051b,c00593,f00613,8000ef,c0001073,40b602b3,128293,4000393
  //   ,729863,50313,fff00393,140006f,b55333,100393,5393b3,fff38393,737533,8067
  //   contents of _18_max3 (hex, n*v repeats v):
  //   513,100593,200613,14000ef,c0001073,b55463,58513,8067,ff810113
  //   ,113023,fedff0ef,50593,60513,fe1ff0ef,13083,810113,8067
  //   contents of _19_fib_rec (hex, n*v repeats v):
  //   40000113,a00513,8000ef,c0001073,100293,a2c463,8067,fe810113,113023
  //   ,a13423,fff50513,fe5ff0ef,a13823,813503,ffe50513,fd5ff0ef,1013303
  //   ,650533,13083,1810113,8067
  //   contents of _20_is_pal (hex, n*v repeats v):
  //   40000113,ff810113,7200293,510023,6100293,5100a3,6300293,510123
  //   ,6500293,5101a3,6300293,510223,6100293,5102a3,7200293,510323,103a3
  //   ,200533,593,600613,8000ef,c0001073,c5c663,100513,3c0006f,b502b3
  //   ,28283,c50333,30303,628663,513,200006f,ff810113,113023,158593
  //   ,fff60613,fc9ff0ef,13083,810113,8067
  //   contents of _21_to_upper (hex, n*v repeats v):
  //   40000113,ff810113,4600293,510023,6f00293,5100a3,6f00293,510123
  //   ,4200293,5101a3,6100293,510223,7200293,5102a3,10323,200533,ff810113
  //   ,2005b3,2004b3,3c000ef,913,293,800313,3800393,2628063,48e03,7e1e33
  //   ,1c96933,148493,128293,ff838393,fe5ff06f,1200533,c0001073,6100313
  //   ,7b00393,50283,2028063,62c663,72d463,fe028293,558023,150513,158593
  //   ,fe1ff06f,58023,8067
  //   contents of _22_sort (hex, n*v repeats v):
  //   40000113,fe010113,200293,512023,800293,512223,600293,512423,400293
  //   ,512623,a00293,512823,c00293,512a23,200533,2004b3,600593,84000ef
  //   ,513,4a283,2029293,556533,44a283,556533,593,84a283,2029293,55e5b3
  //   ,c4a283,55e5b3,613,104a283,2029293,566633,144a283,566633,c0001073
  //   ,e13,293,52303,2be0063,52383,63c663,e0293,38313,1e0e13,450513
  //   ,fe5ff06f,28513,8067,fc810113,113023,293,50313,e13,50e93,6b2d863
  //   ,513423,613823,713c23,3c13023,2a13423,2b13823,30513,405585b3,f91ff0ef
  //   ,50f93,3013583,2813503,2013e03,1813383,1013303,813283,5f8e33,2e1f93
  //   ,1f50eb3,32383,eaf03,7f4663,7ea023,1e32023,128293,430313,f95ff06f
  //   ,13083,3810113,8067
  //   contents of _23_merge_sort (hex, n*v repeats v):
  //   40000113,fe010113,200293,512023,800293,512223,600293,512423,400293
  //   ,512623,a00293,512823,c00293,512a23,200533,2004b3,fe010113,2005b3
  //   ,613,500693,fc000ef,513,4a283,2029293,556533,44a283,556533,593
  //   ,84a283,2029293,55e5b3,c4a283,55e5b3,613,104a283,2029293,566633
  //   ,144a283,566633,c0001073,d602b3,12d293,128293,60313,28393,60e13
  //   ,7c6c463,2e1e93,1d58f33,239713,e50733,72703,231793,f507b3,7a783
  //   ,629863,ef2023,138393,300006f,168813,1039863,ff2023,130313,1c0006f
  //   ,e7d863,ff2023,130313,c0006f,ef2023,138393,1e0e13,f9dff06f,50293
  //   ,58313,60393,76ce63,32e03,1c2a023,428293,430313,138393,fe9ff06f
  //   ,8067,fe010113,113023,2d65e63,d602b3,12d293,513423,c13823,d13c23
  //   ,28693,fddff0ef,813603,160613,1813683,fcdff0ef,1013603,1813683
  //   ,f15ff0ef,13083,2010113,8067
endmodule
