// Digital circuit mem-sd-sw-sb.dig as structural Verilog
module mem_sd_sw_sb (
  input  [63:0] D64in,
  input  [1:0] SZ,
  input  [63:0] ADDR,
  input  [63:0] D64cur,
  output [63:0] Dout
);

  wire [63:0] multiplexer_1_out, multiplexer_2_out;

  Multiplexer #(.Bits(64), .Selector_Bits(3)) multiplexer_1 (
    .sel(ADDR[2:0]), .in_0({D64cur[63:8], D64in[7:0]}), .in_1({D64cur[63:16], D64in[7:0], D64cur[7:0]}),
    .in_2({D64cur[63:24], D64in[7:0], D64cur[15:0]}), .in_3({D64cur[63:32], D64in[7:0], D64cur[23:0]}),
    .in_4({D64cur[63:40], D64in[7:0], D64cur[31:0]}), .in_5({D64cur[63:48], D64in[7:0], D64cur[39:0]}),
    .in_6({D64cur[63:56], D64in[7:0], D64cur[47:0]}), .in_7({D64in[7:0], D64cur[55:0]}),
    .out(multiplexer_1_out));
  Multiplexer #(.Bits(64)) multiplexer_2 (
    .sel(ADDR[2]), .in_0({D64cur[63:32], D64in[31:0]}), .in_1({D64in[31:0], D64cur[31:0]}),
    .out(multiplexer_2_out));
  Multiplexer #(.Bits(64), .Selector_Bits(2)) multiplexer_3 (
    .sel(SZ), .in_0(multiplexer_1_out), .in_1({64{1'b0}}), .in_2(multiplexer_2_out), .in_3(D64in), .out(Dout));

  // Other names for the same wires on the sheet: bindex[2:0] = ADDR[2:0]; windex = ADDR[2]; b0[7:0] = D64cur[7:0];
  //   d1[63:0] = {D64cur[63:16], D64in[7:0], D64cur[7:0]}; d2[63:0] = {D64cur[63:24], D64in[7:0], D64cur[15:0]};
  //   d3[63:0] = {D64cur[63:32], D64in[7:0], D64cur[23:0]}; d4[63:0] = {D64cur[63:40], D64in[7:0], D64cur[31:0]};
  //   d5[63:0] = {D64cur[63:48], D64in[7:0], D64cur[39:0]}; d6[63:0] = {D64cur[63:56], D64in[7:0], D64cur[47:0]};
  //   d7[63:0] = {D64in[7:0], D64cur[55:0]}; w0[31:0] = D64cur[31:0]; b1[7:0] = D64cur[15:8];
  //   d0[63:0] = {D64cur[63:8], D64in[7:0]}; b2[7:0] = D64cur[23:16]; b3[7:0] = D64cur[31:24];
  //   b4[7:0] = D64cur[39:32]; w1[31:0] = D64cur[63:32]; b5[7:0] = D64cur[47:40]; b6[7:0] = D64cur[55:48];
  //   b7[7:0] = D64cur[63:56]; bin[7:0] = D64in[7:0]; win[31:0] = D64in[31:0]
endmodule
