// Digital circuit project07.dig as structural Verilog
module project07 (
  input  [4:0] PROG,
  input  CLK,
  input  CLR,
  input  EN,
  output [63:0] A0,
  output [63:0] A1,
  output [63:0] A2,
  output DONE,
  output [63:0] zero,
  output [63:0] ra,
  output [63:0] sp,
  output [63:0] gp,
  output [63:0] tp,
  output [63:0] t0,
  output [63:0] t1,
  output [63:0] t2,
  output [63:0] s0_fp,
  output [63:0] s1,
  output [63:0] a0_2,
  output [63:0] a1_2,
  output [63:0] a2_2,
  output [63:0] a3,
  output [63:0] a4,
  output [63:0] a5,
  output [63:0] a6,
  output [63:0] a7,
  output [63:0] s2,
  output [63:0] s3,
  output [63:0] s4,
  output [63:0] s5,
  output [63:0] s6,
  output [63:0] s7,
  output [63:0] s8,
  output [63:0] s9,
  output [63:0] s10,
  output [63:0] s11,
  output [63:0] t3,
  output [63:0] t4,
  output [63:0] t5,
  output [63:0] t6
);

  wire ALUA_1, ALUA_2, and_2_out, CLK_t, MLD_1, MLD_2, MLD_3, MR_1, MR_2, MR_3, MR_4, MST_1, MST_2, MST_3,
       PCbr_2, PCbr_3, PCbr_4, PCsl_1, PCsl_2, RFW_1, RFW_2, RFW_3, RFW_4, WDsl_1, WDsl_2, WDsl_3, WDsl_4;
  wire [1:0] MSZ_1, MSZ_2, MSZ_3;
  wire [2:0] ALUB_1, ALUB_2, BUOp_1, BUOp_2;
  wire [3:0] ALOp_1, ALOp_2;
  wire [4:0] RR0_1, RR0_2, RR0_3, RR0_4, RR1_1, RR1_2, RR1_3, RR1_4, WR_1, WR_2, WR_3, WR_4;
  wire [7:0] iw_to_ascii_1_i_0, iw_to_ascii_1_i_1, iw_to_ascii_1_i_2, iw_to_ascii_1_i_3, iw_to_ascii_2_i_0,
       iw_to_ascii_2_i_1, iw_to_ascii_2_i_2, iw_to_ascii_2_i_3, iw_to_ascii_3_i_0, iw_to_ascii_3_i_1,
       iw_to_ascii_3_i_2, iw_to_ascii_3_i_3, iw_to_ascii_4_i_0, iw_to_ascii_4_i_1, iw_to_ascii_4_i_2,
       iw_to_ascii_4_i_3, iw_to_ascii_5_i_0, iw_to_ascii_5_i_1, iw_to_ascii_5_i_2, iw_to_ascii_5_i_3;
  wire [31:0] iw_0, iw_1, iw_2, iw_3, iw_4;
  wire [63:0] _00_if_dr_register_1_pc4_1, _00_if_dr_register_1_pc_1, _01_dr_ex_register_1_pc4_2,
       _01_dr_ex_register_1_pc_2, _01_dr_ex_register_1_rd0_2, _01_dr_ex_register_1_rd1_2,
       _02_ex_mem_register_1_alur_3, _02_ex_mem_register_1_pc4_3, _02_ex_mem_register_1_rd1_3,
       _03_mem_wb_register_1_alur_4, _03_mem_wb_register_1_mrd_4, _03_mem_wb_register_1_pc4_4, alu_1_r,
       decoder_imm_1_imm_b, decoder_imm_1_imm_i, decoder_imm_1_imm_j, decoder_imm_1_imm_s,
       decoder_imm_1_imm_u, decoder_imm_1_shamt, mem_ld_lw_lb_1_d, mem_ld_lw_lb_1_d64cur,
       mem_sd_sw_sb_1_dout, multiplexer_1_out, multiplexer_2_out, multiplexer_3_out, multiplexer_4_out,
       multiplexer_5_out, PC, PC_plus_4_s, ramdualport_1_d, register_file_1_rd0, register_file_1_rd1;

  Multiplexer #(.Bits(64)) multiplexer_1 (
    .sel(PCbr_4), .in_0(PC_plus_4_s), .in_1(multiplexer_5_out), .out(multiplexer_1_out));
  register_with_clr_64bits u_PC (.D(multiplexer_1_out), .CLK(CLK_t), .EN(EN), .CLR(CLR), .Q(PC));
  and and_1 (CLK_t, CLK, ~DONE);  // And
  Comparator #(.Bits(32)) End (.a(iw_4), .b(32'hc0001073), .eq(DONE));  // open: gt, lt
  LED led_1 (.in(DONE));
  Add #(.Bits(64)) PC_plus_4 (.a(PC), .b(64'h4), .c_i(1'b0), .s(PC_plus_4_s));  // open: c_o
  // Probe on iw_to_ascii_1_i_0
  iw_to_ascii iw_to_ascii_1 (
    .I_0(iw_to_ascii_1_i_0), .I_1(iw_to_ascii_1_i_1), .I_2(iw_to_ascii_1_i_2), .I_3(iw_to_ascii_1_i_3),
    .IW(iw_0));
  mem_inst mem_inst_1 (.PROG(PROG), .ADDR(PC[9:2]), .IW(iw_0));
  // Probe on iw_to_ascii_1_i_2
  // Probe on iw_to_ascii_1_i_1
  // Probe on iw_to_ascii_1_i_3
  _00_IF_DR_register _00_if_dr_register_1 (
    .IW_0(iw_0), .PC_0(PC), .PC4_0(PC_plus_4_s), .CLK(CLK_t), .EN(1'b1), .CLR(CLR), .IW_1(iw_1),
    .PC_1(_00_if_dr_register_1_pc_1), .PC4_1(_00_if_dr_register_1_pc4_1));
  decoder_inst decoder_inst_1 (
    .SZ(MSZ_1), .ST(MST_1), .LD(MLD_1), .MR(MR_1), .BUOp(BUOp_1), .WDsel(WDsl_1), .PCsel(PCsl_1),
    .ALUSrcB(ALUB_1), .ALUSrcA(ALUA_1), .ALUOp(ALOp_1), .RFW(RFW_1), .IW(iw_1));
  decoder_reg decoder_reg_1 (.IW(iw_1), .RS1(RR0_1), .RS2(RR1_1), .RD(WR_1));
  Multiplexer #(.Bits(64)) multiplexer_2 (
    .sel(WDsl_4), .in_0(multiplexer_5_out), .in_1(_03_mem_wb_register_1_pc4_4), .out(multiplexer_2_out));
  and and_2 (and_2_out, RFW_4, EN);
  // Probe on iw_to_ascii_2_i_0
  iw_to_ascii iw_to_ascii_2 (
    .I_0(iw_to_ascii_2_i_0), .I_1(iw_to_ascii_2_i_1), .I_2(iw_to_ascii_2_i_2), .I_3(iw_to_ascii_2_i_3),
    .IW(iw_1));
  register_file register_file_1 (
    .RR0(RR0_1), .RR1(RR1_1), .WR(WR_4), .WE(and_2_out), .WD(multiplexer_2_out), .CLK(CLK_t), .CLR(CLR),
    .RD0(register_file_1_rd0), .RD1(register_file_1_rd1), .x0(zero), .x1(ra), .x2(sp), .x3(gp), .x4(tp),
    .x5(t0), .x6(t1), .x7(t2), .x8(s0_fp), .x9(s1), .x10(A0), .x11(A1), .x12(A2), .x13(a3), .x14(a4),
    .x15(a5), .x16(a6), .x17(a7), .x18(s2), .x19(s3), .x20(s4), .x21(s5), .x22(s6), .x23(s7), .x24(s8),
    .x25(s9), .x26(s10), .x27(s11), .x28(t3), .x29(t4), .x30(t6), .x31(t5));
  // Probe on iw_to_ascii_2_i_2
  // Probe on iw_to_ascii_2_i_1
  // Probe on iw_to_ascii_2_i_3
  _01_DR_EX_register _01_dr_ex_register_1 (
    .IW_1(iw_1), .RR0_1(RR0_1), .RR1_1(RR1_1), .WR_1(WR_1), .RD0_1(register_file_1_rd0),
    .RD1_1(register_file_1_rd1), .PC_1(_00_if_dr_register_1_pc_1), .PC4_1(_00_if_dr_register_1_pc4_1),
    .MSZ_1(MSZ_1), .MST_1(MST_1), .MLD_1(MLD_1), .MR_1(MR_1), .BUOp_1(BUOp_1), .WDsl_1(WDsl_1),
    .PCsl_1(PCsl_1), .ALUB_1(ALUB_1), .ALUA_1(ALUA_1), .ALOp_1(ALOp_1), .RFW_1(RFW_1), .CLK(CLK_t),
    .EN(1'b1), .CLR(CLR), .IW_2(iw_2), .RR0_2(RR0_2), .RR1_2(RR1_2), .WR_2(WR_2),
    .RD0_2(_01_dr_ex_register_1_rd0_2), .RD1_2(_01_dr_ex_register_1_rd1_2), .PC_2(_01_dr_ex_register_1_pc_2),
    .PC4_2(_01_dr_ex_register_1_pc4_2), .MSZ_2(MSZ_2), .MST_2(MST_2), .MLD_2(MLD_2), .MR_2(MR_2),
    .BUOp_2(BUOp_2), .WDsl_2(WDsl_2), .PCsl_2(PCsl_2), .ALUB_2(ALUB_2), .ALUA_2(ALUA_2), .ALOp_2(ALOp_2),
    .RFW_2(RFW_2));
  decoder_imm decoder_imm_1 (
    .IW(iw_2), .imm_I(decoder_imm_1_imm_i), .imm_S(decoder_imm_1_imm_s), .imm_B(decoder_imm_1_imm_b),
    .imm_U(decoder_imm_1_imm_u), .imm_J(decoder_imm_1_imm_j), .shamt(decoder_imm_1_shamt));
  // Probe on iw_to_ascii_3_i_0
  iw_to_ascii iw_to_ascii_3 (
    .I_0(iw_to_ascii_3_i_0), .I_1(iw_to_ascii_3_i_1), .I_2(iw_to_ascii_3_i_2), .I_3(iw_to_ascii_3_i_3),
    .IW(iw_2));
  branch_unit branch_unit_1 (
    .A(_01_dr_ex_register_1_rd0_2), .B(_01_dr_ex_register_1_rd1_2), .PCsel(PCsl_2), .BUOp(BUOp_2),
    .PCbr(PCbr_2));
  Multiplexer #(.Bits(64)) multiplexer_3 (
    .sel(ALUA_2), .in_0(_01_dr_ex_register_1_rd0_2), .in_1(_01_dr_ex_register_1_pc_2), .out(multiplexer_3_out));
  Multiplexer #(.Selector_Bits(3), .Bits(64)) multiplexer_4 (
    .sel(ALUB_2), .in_0(_01_dr_ex_register_1_rd1_2), .in_1(decoder_imm_1_imm_i), .in_2(decoder_imm_1_imm_j),
    .in_3(decoder_imm_1_imm_u), .in_4(decoder_imm_1_imm_b), .in_5(decoder_imm_1_shamt),
    .in_6(decoder_imm_1_imm_s), .in_7({64{1'b0}}), .out(multiplexer_4_out));
  // Probe on iw_to_ascii_3_i_2
  // Probe on iw_to_ascii_3_i_1
  // Probe on iw_to_ascii_3_i_3
  alu alu_1 (.A(multiplexer_3_out), .B(multiplexer_4_out), .R(alu_1_r), .ALUop(ALOp_2));
  _02_EX_MEM_register _02_ex_mem_register_1 (
    .IW_2(iw_2), .RR0_2(RR0_2), .RR1_2(RR1_2), .WR_2(WR_2), .ALUR_2(alu_1_r),
    .RD1_2(_01_dr_ex_register_1_rd1_2), .PC4_2(_01_dr_ex_register_1_pc4_2), .MSZ_2(MSZ_2), .MST_2(MST_2),
    .MLD_2(MLD_2), .MR_2(MR_2), .WDsl_2(WDsl_2), .PCbr_2(PCbr_2), .RFW_2(RFW_2), .CLK(CLK_t), .EN(1'b1),
    .CLR(CLR), .IW_3(iw_3), .RR0_3(RR0_3), .RR1_3(RR1_3), .WR_3(WR_3), .ALUR_3(_02_ex_mem_register_1_alur_3),
    .RD1_3(_02_ex_mem_register_1_rd1_3), .PC4_3(_02_ex_mem_register_1_pc4_3), .MSZ_3(MSZ_3), .MST_3(MST_3),
    .MLD_3(MLD_3), .MR_3(MR_3), .WDsl_3(WDsl_3), .PCbr_3(PCbr_3), .RFW_3(RFW_3));
  mem_sd_sw_sb mem_sd_sw_sb_1 (
    .ADDR(_02_ex_mem_register_1_alur_3), .D64in(_02_ex_mem_register_1_rd1_3), .D64cur(mem_ld_lw_lb_1_d64cur),
    .SZ(MSZ_3), .Dout(mem_sd_sw_sb_1_dout));
  RAMDualPort #(.AddrBits(7), .Bits(64)) ramdualport_1 (
    .A(_02_ex_mem_register_1_alur_3[9:3]), .Din(mem_sd_sw_sb_1_dout), .str(MST_3), .C(CLK_t), .ld(MLD_3),
    .D(ramdualport_1_d));
  // Probe on iw_to_ascii_4_i_0
  iw_to_ascii iw_to_ascii_4 (
    .I_0(iw_to_ascii_4_i_0), .I_1(iw_to_ascii_4_i_1), .I_2(iw_to_ascii_4_i_2), .I_3(iw_to_ascii_4_i_3),
    .IW(iw_3));
  // Probe on iw_to_ascii_4_i_2
  // Probe on iw_to_ascii_4_i_1
  mem_ld_lw_lb mem_ld_lw_lb_1 (
    .ADDR(_02_ex_mem_register_1_alur_3), .D64(ramdualport_1_d), .SZ(MSZ_3), .D(mem_ld_lw_lb_1_d),
    .D64cur(mem_ld_lw_lb_1_d64cur));
  // Probe on iw_to_ascii_4_i_3
  _03_MEM_WB_register _03_mem_wb_register_1 (
    .CLK(CLK_t), .EN(1'b1), .CLR(CLR), .IW_4(iw_4), .RR0_4(RR0_4), .RR1_4(RR1_4), .WR_4(WR_4),
    .ALUR_4(_03_mem_wb_register_1_alur_4), .MRD_4(_03_mem_wb_register_1_mrd_4),
    .PC4_4(_03_mem_wb_register_1_pc4_4), .MR_4(MR_4), .WDsl_4(WDsl_4), .PCbr_4(PCbr_4), .RFW_4(RFW_4),
    .IW_3(iw_3), .RR0_3(RR0_3), .RR1_3(RR1_3), .WR_3(WR_3), .ALUR_3(_02_ex_mem_register_1_alur_3),
    .MRD_3(mem_ld_lw_lb_1_d), .PC4_3(_02_ex_mem_register_1_pc4_3), .MR_3(MR_3), .WDsl_3(WDsl_3),
    .PCbr_3(PCbr_3), .RFW_3(RFW_3));
  Multiplexer #(.Bits(64)) multiplexer_5 (
    .sel(MR_4), .in_0(_03_mem_wb_register_1_alur_4), .in_1(_03_mem_wb_register_1_mrd_4),
    .out(multiplexer_5_out));
  // Probe on iw_to_ascii_5_i_0
  iw_to_ascii iw_to_ascii_5 (
    .I_0(iw_to_ascii_5_i_0), .I_1(iw_to_ascii_5_i_1), .I_2(iw_to_ascii_5_i_2), .I_3(iw_to_ascii_5_i_3),
    .IW(iw_4));
  // Probe on iw_to_ascii_5_i_2
  // Probe on iw_to_ascii_5_i_1
  // Probe on iw_to_ascii_5_i_3

  assign a0_2 = A0;
  assign a1_2 = A1;
  assign a2_2 = A2;

  // Other names for the same wires on the sheet: x0[63:0] = zero; x1[63:0] = ra; x2[63:0] = sp; x3[63:0] = gp;
  //   x4[63:0] = tp; x5[63:0] = t0; x6[63:0] = t1; x7[63:0] = t2; x8[63:0] = s0_fp; x9[63:0] = s1; x10[63:0] = A0;
  //   x11[63:0] = A1; x12[63:0] = A2; x13[63:0] = a3; x14[63:0] = a4; x15[63:0] = a5; x16[63:0] = a6; x17[63:0] = a7;
  //   x18[63:0] = s2; x19[63:0] = s3; x20[63:0] = s4; x21[63:0] = s5; x22[63:0] = s6; x23[63:0] = s7; x24[63:0] = s8;
  //   x25[63:0] = s9; x26[63:0] = s10; x27[63:0] = s11; x28[63:0] = t3; x29[63:0] = t4; x30[63:0] = t6;
  //   x31[63:0] = t5

  // Notes on the sheet:
  //   CLK: Hz: 2147483647
  //   (0) IF Stage
  //   Instruction Fetch
  //   (1) DR Stage
  //   Decode Register Read
  //   (2) EX Stage
  //   Execute
  //   (3) MEM Stage
  //   Memory
  //   (4) WB Stage
  //   Write Back
endmodule
