// Digital circuit register-file.dig as structural Verilog
module register_file (
  input  [4:0] RR0,
  input  [4:0] RR1,
  input  CLK,
  input  [4:0] WR,
  input  [63:0] WD,
  input  WE,
  input  CLR,
  output [63:0] RD0,
  output [63:0] RD1,
  output [63:0] x0,
  output [63:0] x1,
  output [63:0] x2,
  output [63:0] x3,
  output [63:0] x4,
  output [63:0] x5,
  output [63:0] x6,
  output [63:0] x7,
  output [63:0] x8,
  output [63:0] x9,
  output [63:0] x10,
  output [63:0] x11,
  output [63:0] x12,
  output [63:0] x13,
  output [63:0] x14,
  output [63:0] x15,
  output [63:0] x16,
  output [63:0] x17,
  output [63:0] x18,
  output [63:0] x19,
  output [63:0] x20,
  output [63:0] x21,
  output [63:0] x22,
  output [63:0] x23,
  output [63:0] x24,
  output [63:0] x25,
  output [63:0] x26,
  output [63:0] x27,
  output [63:0] x28,
  output [63:0] x29,
  output [63:0] x30,
  output [63:0] x31
);

  wire enx1, enx2, enx3, enx4, enx5, enx6, enx7, enx8, enx9, enx10, enx11, enx12, enx13, enx14, enx15, enx16,
       enx17, enx18, enx19, enx20, enx21, enx22, enx23, enx24, enx25, enx26, enx27, enx28, enx29, enx30,
       enx31;
  wire [4:0] multiplexer_1_out;

  Multiplexer #(.Bits(5)) multiplexer_1 (.sel(WE), .in_0({5{1'b0}}), .in_1(WR), .out(multiplexer_1_out));
  Decoder #(.Selector_Bits(5)) decoder_1 (
    .sel(multiplexer_1_out), .out_1(enx1), .out_2(enx2), .out_3(enx3), .out_4(enx4), .out_5(enx5),
    .out_6(enx6), .out_7(enx7), .out_8(enx8), .out_9(enx9), .out_10(enx10), .out_11(enx11), .out_12(enx12),
    .out_13(enx13), .out_14(enx14), .out_15(enx15), .out_16(enx16), .out_17(enx17), .out_18(enx18),
    .out_19(enx19), .out_20(enx20), .out_21(enx21), .out_22(enx22), .out_23(enx23), .out_24(enx24),
    .out_25(enx25), .out_26(enx26), .out_27(enx27), .out_28(enx28), .out_29(enx29), .out_30(enx30),
    .out_31(enx31));  // open: out_0
  register_with_clr_64bits register_with_clr_64bits_1 (.D(WD), .CLK(CLK), .EN(enx1), .CLR(CLR), .Q(x1));
  register_with_clr_64bits register_with_clr_64bits_2 (.D(WD), .CLK(CLK), .EN(enx2), .CLR(CLR), .Q(x2));
  register_with_clr_64bits register_with_clr_64bits_3 (.D(WD), .CLK(CLK), .EN(enx3), .CLR(CLR), .Q(x3));
  register_with_clr_64bits register_with_clr_64bits_4 (.D(WD), .CLK(CLK), .EN(enx4), .CLR(CLR), .Q(x4));
  register_with_clr_64bits register_with_clr_64bits_5 (.D(WD), .CLK(CLK), .EN(enx5), .CLR(CLR), .Q(x5));
  register_with_clr_64bits register_with_clr_64bits_6 (.D(WD), .CLK(CLK), .EN(enx6), .CLR(CLR), .Q(x6));
  register_with_clr_64bits register_with_clr_64bits_7 (.D(WD), .CLK(CLK), .EN(enx7), .CLR(CLR), .Q(x7));
  register_with_clr_64bits register_with_clr_64bits_8 (.D(WD), .CLK(CLK), .EN(enx8), .CLR(CLR), .Q(x8));
  register_with_clr_64bits register_with_clr_64bits_9 (.D(WD), .CLK(CLK), .EN(enx9), .CLR(CLR), .Q(x9));
  register_with_clr_64bits register_with_clr_64bits_10 (.D(WD), .CLK(CLK), .EN(enx10), .CLR(CLR), .Q(x10));
  register_with_clr_64bits register_with_clr_64bits_11 (.D(WD), .CLK(CLK), .EN(enx11), .CLR(CLR), .Q(x11));
  register_with_clr_64bits register_with_clr_64bits_12 (.D(WD), .CLK(CLK), .EN(enx12), .CLR(CLR), .Q(x12));
  register_with_clr_64bits register_with_clr_64bits_13 (.D(WD), .CLK(CLK), .EN(enx13), .CLR(CLR), .Q(x13));
  register_with_clr_64bits register_with_clr_64bits_14 (.D(WD), .CLK(CLK), .EN(enx14), .CLR(CLR), .Q(x14));
  register_with_clr_64bits register_with_clr_64bits_15 (.D(WD), .CLK(CLK), .EN(enx15), .CLR(CLR), .Q(x15));
  register_with_clr_64bits register_with_clr_64bits_16 (.D(WD), .CLK(CLK), .EN(enx16), .CLR(CLR), .Q(x16));
  register_with_clr_64bits register_with_clr_64bits_17 (.D(WD), .CLK(CLK), .EN(enx17), .CLR(CLR), .Q(x17));
  register_with_clr_64bits register_with_clr_64bits_18 (.D(WD), .CLK(CLK), .EN(enx18), .CLR(CLR), .Q(x18));
  register_with_clr_64bits register_with_clr_64bits_19 (.D(WD), .CLK(CLK), .EN(enx19), .CLR(CLR), .Q(x19));
  register_with_clr_64bits register_with_clr_64bits_20 (.D(WD), .CLK(CLK), .EN(enx20), .CLR(CLR), .Q(x20));
  register_with_clr_64bits register_with_clr_64bits_21 (.D(WD), .CLK(CLK), .EN(enx21), .CLR(CLR), .Q(x21));
  register_with_clr_64bits register_with_clr_64bits_22 (.D(WD), .CLK(CLK), .EN(enx22), .CLR(CLR), .Q(x22));
  register_with_clr_64bits register_with_clr_64bits_23 (.D(WD), .CLK(CLK), .EN(enx23), .CLR(CLR), .Q(x23));
  register_with_clr_64bits register_with_clr_64bits_24 (.D(WD), .CLK(CLK), .EN(enx24), .CLR(CLR), .Q(x24));
  register_with_clr_64bits register_with_clr_64bits_25 (.D(WD), .CLK(CLK), .EN(enx25), .CLR(CLR), .Q(x25));
  register_with_clr_64bits register_with_clr_64bits_26 (.D(WD), .CLK(CLK), .EN(enx26), .CLR(CLR), .Q(x26));
  register_with_clr_64bits register_with_clr_64bits_27 (.D(WD), .CLK(CLK), .EN(enx27), .CLR(CLR), .Q(x27));
  register_with_clr_64bits register_with_clr_64bits_28 (.D(WD), .CLK(CLK), .EN(enx28), .CLR(CLR), .Q(x28));
  register_with_clr_64bits register_with_clr_64bits_29 (.D(WD), .CLK(CLK), .EN(enx29), .CLR(CLR), .Q(x29));
  register_with_clr_64bits register_with_clr_64bits_30 (.D(WD), .CLK(CLK), .EN(enx30), .CLR(CLR), .Q(x31));
  register_with_clr_64bits register_with_clr_64bits_31 (.D(WD), .CLK(CLK), .EN(enx31), .CLR(CLR), .Q(x30));
  Multiplexer #(.Selector_Bits(5), .Bits(64)) multiplexer_2 (
    .sel(RR0), .in_0({64{1'b0}}), .in_1(x1), .in_2(x2), .in_3(x3), .in_4(x4), .in_5(x5), .in_6(x6),
    .in_7(x7), .in_8(x8), .in_9(x9), .in_10(x10), .in_11(x11), .in_12(x12), .in_13(x13), .in_14(x14),
    .in_15(x15), .in_16(x16), .in_17(x17), .in_18(x18), .in_19(x19), .in_20(x20), .in_21(x21), .in_22(x22),
    .in_23(x23), .in_24(x24), .in_25(x25), .in_26(x26), .in_27(x27), .in_28(x28), .in_29(x29), .in_30(x31),
    .in_31(x30), .out(RD0));
  Multiplexer #(.Selector_Bits(5), .Bits(64)) multiplexer_3 (
    .sel(RR1), .in_0({64{1'b0}}), .in_1(x1), .in_2(x2), .in_3(x3), .in_4(x4), .in_5(x5), .in_6(x6),
    .in_7(x7), .in_8(x8), .in_9(x9), .in_10(x10), .in_11(x11), .in_12(x12), .in_13(x13), .in_14(x14),
    .in_15(x15), .in_16(x16), .in_17(x17), .in_18(x18), .in_19(x19), .in_20(x20), .in_21(x21), .in_22(x22),
    .in_23(x23), .in_24(x24), .in_25(x25), .in_26(x26), .in_27(x27), .in_28(x28), .in_29(x29), .in_30(x31),
    .in_31(x30), .out(RD1));

  assign x0 = {64{1'b0}};

  // Other names for the same wires on the sheet: x30_t[63:0] = x31; x31_t[63:0] = x30
endmodule
