// Digital circuit register-with-clr-01bits.dig as structural Verilog
module register_with_clr_01bits (
  input  D,
  input  CLK,
  input  CLR,
  input  EN,
  output Q
);

  wire multiplexer_1_out, or_1_out;

  Multiplexer multiplexer_1 (.sel(CLR), .in_0(D), .in_1(1'b0), .out(multiplexer_1_out));
  or or_1 (or_1_out, EN, CLR);
  Register register_1 (.D(multiplexer_1_out), .C(CLK), .en(or_1_out), .Q(Q));
endmodule
