// Digital circuit register-with-clr-02bits.dig as structural Verilog
module register_with_clr_02bits (
  input  [1:0] D,
  input  CLK,
  input  CLR,
  input  EN,
  output [1:0] Q
);

  wire or_1_out;
  wire [1:0] multiplexer_1_out;

  Multiplexer #(.Bits(2)) multiplexer_1 (.sel(CLR), .in_0(D), .in_1(2'b00), .out(multiplexer_1_out));
  or or_1 (or_1_out, EN, CLR);
  Register #(.Bits(2)) register_1 (.D(multiplexer_1_out), .C(CLK), .en(or_1_out), .Q(Q));
endmodule
