// Digital circuit register-with-clr-03bits.dig as structural Verilog
module register_with_clr_03bits (
  input  [2:0] D,
  input  CLK,
  input  CLR,
  input  EN,
  output [2:0] Q
);

  wire or_1_out;
  wire [2:0] multiplexer_1_out;

  Multiplexer #(.Bits(3)) multiplexer_1 (.sel(CLR), .in_0(D), .in_1(3'b000), .out(multiplexer_1_out));
  or or_1 (or_1_out, EN, CLR);
  Register #(.Bits(3)) register_1 (.D(multiplexer_1_out), .C(CLK), .en(or_1_out), .Q(Q));
endmodule
