// Digital circuit register-with-clr-04bits.dig as structural Verilog
module register_with_clr_04bits (
  input  [3:0] D,
  input  CLK,
  input  CLR,
  input  EN,
  output [3:0] Q
);

  wire or_1_out;
  wire [3:0] multiplexer_1_out;

  Multiplexer #(.Bits(4)) multiplexer_1 (.sel(CLR), .in_0(D), .in_1(4'b0000), .out(multiplexer_1_out));
  or or_1 (or_1_out, EN, CLR);
  Register #(.Bits(4)) register_1 (.D(multiplexer_1_out), .C(CLK), .en(or_1_out), .Q(Q));
endmodule
